# Fritzing sketch PCB (saved by Fritzing 0.9.3b)
circuit board: 2cm x 6.3cm
breadboards: 1

parts:
  Relay = OMRON PCB Power Relay – G5LE [part_number="G5LE-1\n" package=THT]
  Accelerometer = female pin header, 5 pins [form="♀ (female)"]
  Solenoid = female pin header, 2 pins [form="♀ (female)"]
  Nano = Arduino Nano (Rev3.0)
  R1 = Resistor [tolerance=±5% resistance=220 package=THT]
  R2 = Resistor [tolerance=±5% resistance=220 package=THT]
  J1 = Piezo Speaker

nets:
  N1: Relay.A, Solenoid.pin2
  N2: Relay.COIL1, Accelerometer.pin2, Nano.GND, J1.pin1
  N3: Relay.C, Solenoid.pin1
  N4: Relay.COIL2, Nano.D5
  N5: Accelerometer.pin1, Nano.3V3
  N6: Accelerometer.pin3, Nano.A5
  N7: Accelerometer.pin4, Nano.A4
  N8: Nano.D6, R1.Pin_0, R2.Pin_0
  N9: R1.Pin_1, R2.Pin_1, J1.pin2
