# Fritzing sketch FinalPCB (saved by Fritzing 0.9.3b)
circuit board: 8.46667cm x 5.64444cm
breadboards: 1

parts:
  Sensor = Adafruit TSL2561 Digital Luminosity/Lux/Light Sensor
  Arduino = Arduino Uno (Rev3)
  LED1 = LED - 3mm [color="Red (633nm)" package="3 mm [THT]"]
  LED2 = LED - 3mm [color="Red (633nm)" package="3 mm [THT]"]
  Motor_Driver = L293D [package=THT]
  Motor = DC Motor
  Resistor = Resistor [tolerance=±5% resistance=220 package=THT]

nets (from the schematic view):
  N1: Sensor.SCL, Arduino.A5/SCL
  N2: Sensor.SDA, Arduino.A4/SDA
  GND: Sensor.GND, Arduino.GND, Motor_Driver.0V, Resistor.Pin_0
  VIN: Sensor.VIN, Arduino.3V3
  N3: Arduino.D9_PWM, Motor_Driver.In_2
  N4: Arduino.D10_PWM/SS, Motor_Driver.In_1
  N5: Arduino.D11_PWM/MOSI, Motor_Driver.Enable_1
  N6: Arduino.D6_PWM, LED1.anode, LED2.anode
  N7: Arduino.5V, Motor_Driver.+Vmotor, Motor_Driver.+V
  N8: LED1.cathode, LED2.cathode, Resistor.Pin_1
  N9: Motor_Driver.Out_1_(_Controlled_by_Enable_1_), Motor.pin_2
  N10: Motor_Driver.Out_2_(_Controlled_by_Enable_1_), Motor.pin_1
